// Digital circuit MUX.dig as structural Verilog
module MUX (
  input  D,
  input  C,
  input  B,
  input  A,
  output Y
);

  wire not_1_out;

  not not_1 (not_1_out, D);
  Multiplexer #(.Selector_Bits(3)) multiplexer_1 (
    .sel({A, 2'b00}), .in_0(D), .in_1(1'b0), .in_2(1'b0), .in_3(1'b0), .in_4(not_1_out), .in_5(1'b0),
    .in_6(1'b0), .in_7(1'b0), .out(Y));

  // Notes on the sheet:
  //   Use A as the most-significant bit and 
  //   D as the least-significant bit.
  //   Converts between single bits & a 3-bit bus
endmodule

/* Test case:
A B C D Y
0 0 0 0 X
0 0 0 1 1
*/
